# Fritzing sketch Untitled Sketch 3 (saved by Fritzing 0.9.4)
breadboards: 1

parts:
  R2 = Trimmer Potentiometer [maximum_resistance=10kΩ package=THT]
  Bauteil1 = Arduino Uno (Rev3)
  J1 = Basic Servo

nets:
  N1: R2.leg1, J1.vcc
  N2: R2.wiper, Bauteil1.A1
  GND: R2.leg2, Bauteil1.GND, J1.gnd
  N3: Bauteil1.D3_PWM, J1.pulse

notes:
  5V Anschluss
